// Logisim project 4way traffic control system.circ as structural Verilog: 2 circuits, main circuit main
module main (
);

  wire and_1_out, and_2_out, clock_1_out, d_ff_1_q, d_ff_1_qn, d_ff_2_q, d_ff_2_qn, nor_1_out, nor_2_out,
       or_1_out, or_2_out, submodule_1_out_4, xor_1_out;

  submodule submodule_1 (.in_1(d_ff_1_q), .in_2(d_ff_2_q), .in_3(1'b1), .out_4(submodule_1_out_4));
  xor xor_1 (xor_1_out, 1'b1, d_ff_2_q);
  Clock clock_1 (.out(clock_1_out));
  D_Flip_Flop d_ff_1 (
    .clk(clock_1_out), .D(submodule_1_out_4), .Q(d_ff_1_q), .Qn(d_ff_1_qn));  // open: preset, en, reset
  D_Flip_Flop d_ff_2 (.clk(clock_1_out), .D(xor_1_out), .Q(d_ff_2_q), .Qn(d_ff_2_qn));  // open: preset, en, reset
  and and_1 (and_1_out, d_ff_1_q, d_ff_2_qn);
  nor nor_1 (nor_1_out, d_ff_1_qn, d_ff_2_qn);
  and and_2 (and_2_out, d_ff_1_qn, d_ff_2_q);
  nor nor_2 (nor_2_out, d_ff_2_q, d_ff_1_q);
  LED led_1 (.in(or_1_out));
  LED led_2 (.in(and_1_out));
  LED led_3 (.in(nor_1_out));
  or or_1 (or_1_out, and_2_out, nor_2_out);
  or or_2 (or_2_out, and_1_out, nor_1_out);
  LED led_4 (.in(or_2_out));
  LED led_5 (.in(nor_2_out));
  LED led_6 (.in(and_2_out));
  LED led_7 (.in(or_2_out));
  LED led_8 (.in(nor_2_out));
  LED led_9 (.in(and_2_out));
  LED led_10 (.in(or_1_out));
  LED led_11 (.in(and_1_out));
  LED led_12 (.in(nor_1_out));

  // Notes on the sheet:
  //   Swiching Theory lab Logisim project
  //   ( 1701CS12 )
  //   Submodule
  //   West
  //   4 way Traffic Control System
  //   North
  //   South
  //   East
endmodule

module submodule (
  input  in_1,
  input  in_2,
  input  in_3,
  output out_4
);

  wire and_1_out, and_2_out, and_3_out, not_1_out, not_2_out, not_3_out;

  not not_1 (not_1_out, in_3);
  and and_1 (and_1_out, in_1, in_2);
  not not_2 (not_2_out, in_1);
  not not_3 (not_3_out, in_2);
  and and_2 (and_2_out, in_1, not_1_out);
  and and_3 (and_3_out, not_2_out, in_3, not_3_out);
  or or_1 (out_4, and_1_out, and_3_out, and_2_out);
endmodule
